# Fritzing sketch Шаблон электросхемы проекта (saved by Fritzing 0.9.3b)
breadboards: 1

parts:
  Часть1 = Arduino Uno (Rev3)
  VCC1 = Battery
  S1 = Toggle Switch [package=THT]
  S3 = Pushbutton [package="[THT]"]
  S4 = Pushbutton [package="[THT]"]
  S5 = Pushbutton [package="[THT]"]
  S6 = Pushbutton [package="[THT]"]
  S7 = Pushbutton [package="[THT]"]
  S8 = Pushbutton [package="[THT]"]
  S9 = Pushbutton [package="[THT]"]
  S10 = Pushbutton [package="[THT]"]
  SP1 = SPEAKER [package=pcb_mount_speaker]
  Disp1 = LBT2088AH [part_number=LBT2088AH]
  Q1 = NPN-Transistor [package="TO92 [THT]"]

nets:
  N1: Часть1.D8, S5.Pin_3, S5.Pin_4
  N2: Часть1.D9_PWM, S6.Pin_3, S6.Pin_4
  N3: Часть1.D10_PWM/SS, Disp1.pin_14
  N4: Часть1.D11_PWM/MOSI, Q1.B
  N5: Часть1.D2, S9.Pin_3, S9.Pin_4
  N6: Часть1.D3_PWM, S7.Pin_3, S7.Pin_4
  N7: Часть1.D4, S3.Pin_3, S3.Pin_4
  N8: Часть1.D5_PWM, S4.Pin_3, S4.Pin_4
  N9: Часть1.D6_PWM, S10.Pin_3, S10.Pin_4
  N10: Часть1.D7, S8.Pin_3, S8.Pin_4
  N11: Часть1.GND, S1.L2, S3.Pin_1, S3.Pin_2, S4.Pin_1, S4.Pin_2, S5.Pin_1, S5.Pin_2, S6.Pin_1, S6.Pin_2, S7.Pin_1, S7.Pin_2, S8.Pin_1, S8.Pin_2, S9.Pin_1, S9.Pin_2, S10.Pin_1, S10.Pin_2, SP1.+, Disp1.pin_15
  N12: Часть1.VIN, VCC1.+, Disp1.pin_16, Q1.E
  N13: VCC1.-, S1.L1
  N14: SP1.-, Q1.C
